// Logisim project Arquivo Principal.circ as structural Verilog: 1 circuit, main circuit main
module main (
  input  in_1,
  input  A3,
  input  A2,
  input  A1,
  input  A0,
  input  B3,
  input  B2,
  input  B1,
  input  B0,
  input  in_10,
  output S4,
  output S3,
  output S2,
  output S1,
  output S0
);

  wire main_1_a_2, main_1_b_2, main_1_c_2, main_1_d_2, main_1_e_2, main_1_f, main_1_g, main_2_a_2,
       main_2_b_2, main_2_c_2, main_2_d_2, main_2_e, main_2_f, main_2_g, main_3_a_2, main_3_b_2, main_3_c_2,
       main_3_d_2, main_3_e_2, main_3_f, main_3_g, main_4_a_2, main_4_b_2, main_4_c_2, main_4_d_2,
       main_4_e_2, main_4_f, main_4_g, main_5_a_2, main_5_b_2, main_5_c_2, main_5_d_2, main_5_e, main_5_f,
       main_5_g, main_6_a_2, main_6_b_2, main_6_c_2, main_6_d_2, main_6_e_2, main_6_f, main_6_g, ms_1_co,
       sc_2_co, sc_3_co;

  SEGUNDO_DIGITO_main main_1 (
    .A(in_1), .B(A3), .C(A2), .D(A1), .E(A0), .A_2(main_1_a_2), .B_2(main_1_b_2), .C_2(main_1_c_2),
    .D_2(main_1_d_2), .E_2(main_1_e_2), .F(main_1_f), .G(main_1_g));
  \decocificador_comp___Cópia_main  main_2 (
    .A(A3), .B(A2), .C(A1), .D(A0), .A_2(main_2_a_2), .B_2(main_2_b_2), .C_2(main_2_c_2), .D_2(main_2_d_2),
    .E(main_2_e), .F(main_2_f), .G(main_2_g));
  _7_Segment_Display u_7_segment_display_1 (
    .g(main_1_g), .f(main_1_f), .a(main_1_a_2), .b(main_1_b_2), .e(main_1_e_2), .d(main_1_d_2), .c(main_1_c_2));  // open: dp
  _7_Segment_Display u_7_segment_display_2 (
    .g(main_2_g), .f(main_2_f), .a(main_2_a_2), .b(main_2_b_2), .e(main_2_e), .d(main_2_d_2), .c(main_2_c_2));  // open: dp
  SC sc_1 (.A(A3), .B(B3), .Cin(sc_2_co), .Co(S4), .S(S3));
  SEGUNDO_DIGITO_main main_3 (
    .A(S4), .B(S3), .C(S2), .D(S1), .E(S0), .A_2(main_3_a_2), .B_2(main_3_b_2), .C_2(main_3_c_2),
    .D_2(main_3_d_2), .E_2(main_3_e_2), .F(main_3_f), .G(main_3_g));
  SC sc_2 (.A(A2), .B(B2), .Cin(sc_3_co), .Co(sc_2_co), .S(S2));
  _7_Segment_Display u_7_segment_display_3 (
    .g(main_3_g), .f(main_3_f), .a(main_3_a_2), .b(main_3_b_2), .e(main_3_e_2), .d(main_3_d_2), .c(main_3_c_2));  // open: dp
  SC sc_3 (.A(A1), .B(B1), .Cin(ms_1_co), .Co(sc_3_co), .S(S1));
  decocificador_comp_resultado_main main_4 (
    .A(S4), .B(S3), .C(S2), .D(S1), .E(S0), .A_2(main_4_a_2), .B_2(main_4_b_2), .C_2(main_4_c_2),
    .D_2(main_4_d_2), .E_2(main_4_e_2), .F(main_4_f), .G(main_4_g));
  _7_Segment_Display u_7_segment_display_4 (
    .g(main_4_g), .f(main_4_f), .a(main_4_a_2), .b(main_4_b_2), .e(main_4_e_2), .d(main_4_d_2), .c(main_4_c_2));  // open: dp
  MS ms_1 (.A(A0), .B(B0), .CO(ms_1_co), .S(S0));
  \decocificador_comp___Cópia_main  main_5 (
    .A(B3), .B(B2), .C(B1), .D(B0), .A_2(main_5_a_2), .B_2(main_5_b_2), .C_2(main_5_c_2), .D_2(main_5_d_2),
    .E(main_5_e), .F(main_5_f), .G(main_5_g));
  _7_Segment_Display u_7_segment_display_5 (
    .g(main_6_g), .f(main_6_f), .a(main_6_a_2), .b(main_6_b_2), .e(main_6_e_2), .d(main_6_d_2), .c(main_6_c_2));  // open: dp
  _7_Segment_Display u_7_segment_display_6 (
    .g(main_5_g), .f(main_5_f), .a(main_5_a_2), .b(main_5_b_2), .e(main_5_e), .d(main_5_d_2), .c(main_5_c_2));  // open: dp
  SEGUNDO_DIGITO_main main_6 (
    .A(in_10), .B(B3), .C(B2), .D(B1), .E(B0), .A_2(main_6_a_2), .B_2(main_6_b_2), .C_2(main_6_c_2),
    .D_2(main_6_d_2), .E_2(main_6_e_2), .F(main_6_f), .G(main_6_g));

  // Notes on the sheet:
  //   SOMA (RESULTADO)
  //   16
  //   4
  //   ENTRADA B (número 2)
  //   2
  //   1
endmodule
