// Logisim project DISPLAYRES.circ as structural Verilog: 1 circuit, main circuit main
module main (
  input  A,
  input  B,
  input  C,
  input  D,
  input  E,
  output A_2,
  output B_2,
  output C_2,
  output D_2,
  output E_2,
  output F,
  output G
);

  wire and_1_out, and_2_out, and_3_out, and_4_out, and_5_out, and_6_out, and_7_out, and_8_out, and_9_out,
       and_10_out, and_11_out, and_12_out, and_13_out, and_14_out, and_15_out, and_16_out, and_17_out,
       and_18_out, and_19_out, and_20_out, and_21_out, and_22_out, and_23_out, and_24_out, and_25_out,
       and_26_out, and_27_out, and_28_out, and_29_out, and_30_out, and_31_out, not_1_out, not_2_out,
       not_3_out, not_4_out, not_5_out;

  not not_1 (not_1_out, A);
  not not_2 (not_2_out, B);
  not not_3 (not_3_out, D);
  not not_4 (not_4_out, C);
  not not_5 (not_5_out, E);
  and and_1 (and_1_out, A, not_4_out, E);
  and and_2 (and_2_out, A, C, not_5_out);
  and and_3 (and_3_out, A, not_2_out, D);
  and and_4 (and_4_out, A, B, not_3_out, E);
  and and_5 (and_5_out, A, not_2_out, C);
  and and_6 (and_6_out, A, C, not_3_out);
  and and_7 (and_7_out, A, not_2_out, E);
  and and_8 (and_8_out, A, not_2_out, D);
  and and_9 (and_9_out, A, C, not_5_out);
  and and_10 (and_10_out, A, not_4_out, D, E);
  and and_11 (and_11_out, A, B, not_3_out, not_5_out);
  and and_12 (and_12_out, A, not_3_out);
  and and_13 (and_13_out, A, not_4_out);
  and and_14 (and_14_out, A, B, not_5_out);
  and and_15 (and_15_out, A, not_2_out, E);
  and and_16 (and_16_out, A, D, not_5_out);
  and and_17 (and_17_out, A, not_2_out, not_5_out);
  and and_18 (and_18_out, A, B, not_4_out, not_3_out, E);
  and and_19 (and_19_out, A, B, C, not_5_out);
  and and_20 (and_20_out, A, not_2_out, D, E);
  and and_21 (and_21_out, A, D, not_5_out);
  and and_22 (and_22_out, A, not_2_out, not_5_out);
  and and_23 (and_23_out, A, C, not_5_out);
  and and_24 (and_24_out, A, not_3_out, not_5_out);
  and and_25 (and_25_out, A, not_4_out, not_5_out);
  and and_26 (and_26_out, A, B, not_3_out);
  and and_27 (and_27_out, A, B, not_5_out);
  and and_28 (and_28_out, A, not_2_out, not_4_out, D);
  and and_29 (and_29_out, A, B, not_3_out);
  and and_30 (and_30_out, A, not_2_out, D);
  and and_31 (and_31_out, A, not_4_out, not_5_out);
  or or_1 (A_2, and_1_out, and_2_out, and_3_out, and_4_out);
  or or_2 (C_2, and_12_out, and_13_out, and_14_out, and_15_out);
  or or_3 (D_2, and_16_out, and_17_out, and_20_out, and_18_out, and_19_out);
  or or_4 (F, and_24_out, and_25_out, and_26_out, and_27_out, and_28_out);
  or or_5 (G, and_29_out, and_30_out, and_31_out);
  or or_6 (B_2, and_5_out, and_6_out, and_7_out, and_8_out, and_9_out, and_10_out, and_11_out);
  or or_7 (E_2, and_21_out, and_22_out, and_23_out);
  _7_Segment_Display u_7_segment_display_1 (.g(G), .f(F), .a(A_2), .b(B_2), .e(E_2), .d(D_2), .c(C_2));  // open: dp
endmodule
