// Logisim project SEGUNDO_DIGITO.circ as structural Verilog: 1 circuit, main circuit main
module main (
  input  A,
  input  B,
  input  C,
  input  D,
  input  E,
  output A_2,
  output B_2,
  output C_2,
  output D_2,
  output E_2,
  output F,
  output G
);

  wire and_1_out, and_2_out, and_3_out, and_4_out, and_5_out, and_6_out, and_7_out, and_8_out, not_1_out,
       not_2_out, not_3_out, not_4_out, not_5_out, or_1_out, or_2_out, or_3_out;

  not not_1 (not_1_out, A);
  not not_2 (not_2_out, B);
  not not_3 (not_3_out, C);
  not not_4 (not_4_out, D);
  not not_5 (not_5_out, E);
  and and_1 (and_1_out, D, not_1_out, B, not_3_out);
  and and_2 (and_2_out, not_1_out, B, C);
  and and_3 (and_3_out, A, not_2_out, not_3_out);
  and and_4 (and_4_out, A, not_2_out, C);
  and and_5 (and_5_out, A, B, not_3_out);
  and and_6 (and_6_out, A, B, C);
  and and_7 (and_7_out, A, B, C, D);
  or or_1 (or_1_out, and_1_out, and_2_out, and_3_out);
  or or_2 (or_2_out, and_4_out, and_5_out, and_6_out);
  or or_3 (or_3_out, or_1_out, and_7_out);
  and and_8 (and_8_out, and_7_out, or_2_out, or_1_out);
  decocificador_comp_main main_1 (
    .A(and_8_out), .B(and_8_out), .C(or_2_out), .D(or_3_out), .a_2(A_2), .b_2(B_2), .c_2(C_2), .d_2(D_2),
    .e(E_2), .f(F), .g(G));
endmodule
