// Logisim project decocificador comp - Cópia.circ as structural Verilog: 1 circuit, main circuit main
module main (
  input  A,
  input  B,
  input  C,
  input  D,
  output A_2,
  output B_2,
  output C_2,
  output D_2,
  output E,
  output F,
  output G
);

  wire and_1_out, and_2_out, and_3_out, and_4_out, and_5_out, and_6_out, and_7_out, and_8_out, and_9_out,
       and_10_out, and_11_out, and_12_out, and_13_out, and_14_out, and_15_out, and_16_out, and_17_out,
       and_18_out, and_19_out, and_20_out, and_21_out, and_22_out, and_23_out, and_24_out, and_25_out,
       and_26_out, and_27_out, and_28_out, and_29_out, and_30_out, and_31_out, and_32_out, and_33_out,
       and_34_out, and_35_out, and_36_out, and_37_out, and_38_out, and_39_out, and_40_out, and_41_out,
       not_1_out, not_2_out, not_3_out, not_4_out, not_5_out, or_1_out, or_2_out, or_3_out, or_4_out,
       or_5_out, or_6_out, or_7_out, or_8_out, or_9_out, or_10_out, or_11_out, or_12_out, or_13_out, undriven;

  not not_1 (not_1_out, undriven);
  not not_2 (not_2_out, A);
  not not_3 (not_3_out, B);
  not not_4 (not_4_out, C);
  not not_5 (not_5_out, D);
  and and_1 (and_1_out, not_2_out, B, D);
  and and_2 (and_2_out, not_2_out, not_3_out, not_5_out);
  and and_3 (and_3_out, not_2_out, C, D);
  and and_4 (and_4_out, A, not_3_out, not_4_out);
  and and_5 (and_5_out, not_2_out, not_3_out);
  and and_6 (and_6_out, not_3_out, not_4_out);
  and and_7 (and_7_out, not_2_out, not_4_out, not_5_out);
  and and_8 (and_8_out, not_2_out, C, D);
  and and_9 (and_9_out, not_2_out, B);
  and and_10 (and_10_out, not_3_out, not_4_out);
  and and_11 (and_11_out, not_2_out, D);
  and and_12 (and_12_out, not_3_out, not_4_out, not_5_out);
  and and_13 (and_13_out, not_2_out, not_3_out, C);
  and and_14 (and_14_out, not_2_out, C, not_5_out);
  and and_15 (and_15_out, not_2_out, B, not_4_out, D);
  and and_16 (and_16_out, not_3_out, not_4_out, not_5_out);
  and and_17 (and_17_out, not_2_out, C, not_5_out);
  and and_18 (and_18_out, not_2_out, B, not_4_out);
  and and_19 (and_19_out, A, not_3_out, not_4_out);
  and and_20 (and_20_out, not_2_out, B, not_5_out);
  and and_21 (and_21_out, not_3_out, not_4_out, not_5_out);
  and and_22 (and_22_out, A, not_3_out, not_4_out);
  and and_23 (and_23_out, not_2_out, B, not_4_out);
  and and_24 (and_24_out, not_2_out, not_3_out, C);
  and and_25 (and_25_out, not_2_out, C, not_5_out);
  and and_26 (and_26_out, A, B, D);
  and and_27 (and_27_out, A, B, not_4_out);
  and and_28 (and_28_out, A, B, D);
  and and_29 (and_29_out, A, not_3_out, C, not_5_out);
  and and_30 (and_30_out, A, B, not_4_out, not_5_out);
  and and_31 (and_31_out, A, C, not_5_out);
  and and_32 (and_32_out, A, B, C);
  and and_33 (and_33_out, A, B);
  or or_1 (or_1_out, and_1_out, and_2_out, and_3_out, and_4_out);
  or or_2 (or_2_out, and_5_out, and_6_out, and_7_out, and_8_out);
  or or_3 (or_3_out, and_16_out, and_17_out);
  or or_4 (or_4_out, and_18_out, and_19_out, and_20_out, and_21_out);
  and and_34 (and_34_out, A, B, not_4_out);
  and and_35 (and_35_out, A, not_3_out, C, not_5_out);
  and and_36 (and_36_out, A, not_3_out, C);
  and and_37 (and_37_out, A, B, not_4_out);
  and and_38 (and_38_out, A, B, not_5_out);
  and and_39 (and_39_out, A, C);
  and and_40 (and_40_out, A, B, D);
  and and_41 (and_41_out, A, not_3_out, C, not_5_out);
  or or_5 (or_5_out, and_9_out, and_10_out, and_11_out);
  or or_6 (or_6_out, and_12_out, and_13_out, and_14_out, and_15_out);
  or or_7 (or_7_out, and_22_out, and_23_out, and_24_out, and_25_out);
  or or_8 (or_8_out, and_36_out, and_37_out, and_38_out);
  or or_9 (or_9_out, and_39_out, and_40_out);
  or or_10 (or_10_out, and_29_out, and_30_out);
  or or_11 (or_11_out, and_31_out, and_32_out);
  or or_12 (or_12_out, and_34_out, and_26_out, and_35_out);
  or or_13 (or_13_out, and_27_out, and_28_out, and_41_out);
  _7_Segment_Display u_7_segment_display_1 (
    .g(or_7_out), .f(or_4_out), .a(or_1_out), .b(or_2_out), .e(or_3_out), .d(or_6_out), .c(or_5_out));  // open: dp
  _7_Segment_Display u_7_segment_display_2 (
    .g(and_33_out), .f(or_11_out), .a(or_12_out), .b(or_8_out), .e(or_10_out), .d(or_13_out), .c(or_9_out));  // open: dp
  or or_14 (A_2, or_1_out, or_12_out);
  or or_15 (B_2, or_2_out, or_8_out);
  or or_16 (C_2, or_5_out, or_9_out);
  or or_17 (D_2, or_6_out, or_13_out);
  or or_18 (E, or_3_out, or_10_out);
  or or_19 (F, or_4_out, or_11_out);
  or or_20 (G, or_7_out, and_33_out);

  // Notes on the sheet:
  //   SEGMENTOS
endmodule
