// Logisim project meio_somador.circ as structural Verilog: 1 circuit, main circuit MS
module MS (
  input  A,
  input  B,
  output CO,
  output S
);

  wire and_2_out, and_3_out, not_1_out, not_2_out;

  not not_1 (not_1_out, A);
  not not_2 (not_2_out, B);
  and and_1 (CO, A, B);
  and and_2 (and_2_out, A, not_2_out);
  and and_3 (and_3_out, not_1_out, B);
  or or_1 (S, and_2_out, and_3_out);

  // Notes on the sheet:
  //   CIRCUITO MEIO SOMADOR - HALF ADDER
  //   Vai Um
endmodule
