// Logisim project somador_completo.circ as structural Verilog: 1 circuit, main circuit SC
module SC (
  input  A,
  input  B,
  input  Cin,
  output Co,
  output S
);

  wire and_1_out, and_2_out, and_3_out, and_4_out, and_5_out, and_6_out, and_7_out, not_1_out, not_2_out,
       not_3_out;

  not not_1 (not_1_out, B);
  not not_2 (not_2_out, A);
  not not_3 (not_3_out, Cin);
  and and_1 (and_1_out, A, B);
  and and_2 (and_2_out, A, Cin);
  and and_3 (and_3_out, B, Cin);
  and and_4 (and_4_out, not_2_out, not_1_out, Cin);
  and and_5 (and_5_out, not_2_out, B, not_3_out);
  and and_6 (and_6_out, A, not_1_out, not_3_out);
  and and_7 (and_7_out, A, B, Cin);
  or or_1 (Co, and_1_out, and_2_out, and_3_out);
  or or_2 (S, and_4_out, and_5_out, and_6_out, and_7_out);
endmodule
